// Logisim project ep2.circ as structural Verilog: 12 circuits, main circuit main
module main (
  input  a7,
  input  s2,
  input  s1,
  input  s0,
  input  a6,
  input  a5,
  input  a4,
  input  a3,
  input  a2,
  input  a1,
  input  a0,
  input  b7,
  input  b6,
  input  b5,
  input  b4,
  input  b3,
  input  b2,
  input  b1,
  input  b0,
  output r7,
  output r6,
  output r5,
  output r4,
  output r3,
  output r2,
  output r1,
  output r0,
  output Overflow
);

  wire clock_1_out;

  Clock clock_1 (.out(clock_1_out));
  ALU alu_1 (
    .a7(a7), .a6(a6), .a5(a5), .a4(a4), .a3(a3), .a2(a2), .a1(a1), .a0(a0), .b7(b7), .b6(b6), .b5(b5),
    .b4(b4), .b3(b3), .b2(b2), .b1(b1), .b0(b0), .overflow(Overflow), .s2(s2), .s1(s1), .s0(s0), .r7(r7),
    .r6(r6), .r5(r5), .r4(r4), .r3(r3), .r2(r2), .r1(r1), .r0(r0), .Clock(clock_1_out));

  // Notes on the sheet:
  //   > Daniel Toshio Iwamoto      - nº USP: 8516782
  //   > Gustavo Chicato Wandeur - nº USP: 7557797
  //   > Leonardo Pereira Macedo - nº USP: 8536065
  //   Componentes do grupo:
  //   EP2 - Algebra Booleana
  //   Professor: Junior Barrera
endmodule

module ALU (
  input  s2,
  input  s1,
  input  s0,
  input  a7,
  input  a6,
  input  a5,
  input  a4,
  input  a3,
  input  a2,
  input  a1,
  input  a0,
  input  b7,
  input  b6,
  input  b5,
  input  b4,
  input  b3,
  input  b2,
  input  b1,
  input  b0,
  input  Clock,
  output overflow,
  output r7,
  output r6,
  output r5,
  output r4,
  output r3,
  output r2,
  output r1,
  output r0
);

  wire DivZero, OverMult, OverSoma, OverSub;
  wire [7:0] \divisão_1_q0 , \divisão_1_r0 , \multiplicação_1_r0 , soma_1_r0, \subtração_1_r0 ;

  Soma soma_1 (
    .r7(soma_1_r0[7]), .r6(soma_1_r0[6]), .r5(soma_1_r0[5]), .r4(soma_1_r0[4]), .r3(soma_1_r0[3]),
    .r2(soma_1_r0[2]), .r1(soma_1_r0[1]), .r0(soma_1_r0[0]), .a7(a7), .a6(a6), .a5(a5), .a4(a4), .a3(a3),
    .a2(a2), .a1(a1), .a0(a0), .b7(b7), .b6(b6), .b5(b5), .b4(b4), .b3(b3), .b2(b2), .b1(b1), .b0(b0),
    .Overflow(OverSoma));
  \Subtração  \subtração_1  (
    .a7(a7), .a6(a6), .a5(a5), .a4(a4), .a3(a3), .a2(a2), .a1(a1), .a0(a0), .b7(b7), .b6(b6), .b5(b5),
    .b4(b4), .b3(b3), .b2(b2), .b1(b1), .b0(b0), .r7(\subtração_1_r0 [7]), .r6(\subtração_1_r0 [6]),
    .r5(\subtração_1_r0 [5]), .r4(\subtração_1_r0 [4]), .r3(\subtração_1_r0 [3]), .r2(\subtração_1_r0 [2]),
    .r1(\subtração_1_r0 [1]), .r0(\subtração_1_r0 [0]), .Overflow(OverSub));
  \Multiplicação  \multiplicação_1  (
    .a7(a7), .a6(a6), .a5(a5), .a4(a4), .a3(a3), .a2(a2), .a1(a1), .a0(a0), .r7(\multiplicação_1_r0 [7]),
    .r6(\multiplicação_1_r0 [6]), .r5(\multiplicação_1_r0 [5]), .r4(\multiplicação_1_r0 [4]),
    .r3(\multiplicação_1_r0 [3]), .r2(\multiplicação_1_r0 [2]), .r1(\multiplicação_1_r0 [1]),
    .r0(\multiplicação_1_r0 [0]), .Overflow(OverMult), .b7(b7), .b6(b6), .b5(b5), .b4(b4), .b3(b3), .b2(b2),
    .b1(b1), .b0(b0), .Clock(Clock));
  \Divisão  \divisão_1  (
    .\Divisão_por_zero (DivZero), .a7(a7), .a6(a6), .a5(a5), .a4(a4), .a3(a3), .a2(a2), .a1(a1), .a0(a0),
    .b7(b7), .b6(b6), .b5(b5), .b4(b4), .b3(b3), .b2(b2), .b1(b1), .r7(\divisão_1_r0 [7]), .b0(b0),
    .r6(\divisão_1_r0 [6]), .r5(\divisão_1_r0 [5]), .r4(\divisão_1_r0 [4]), .r3(\divisão_1_r0 [3]),
    .r2(\divisão_1_r0 [2]), .r1(\divisão_1_r0 [1]), .r0(\divisão_1_r0 [0]), .q7(\divisão_1_q0 [7]),
    .q6(\divisão_1_q0 [6]), .q5(\divisão_1_q0 [5]), .q4(\divisão_1_q0 [4]), .q3(\divisão_1_q0 [3]),
    .q2(\divisão_1_q0 [2]), .q1(\divisão_1_q0 [1]), .q0(\divisão_1_q0 [0]), .Clock(Clock));
  Multiplexer #(.select(3), .width(8), .enable("false")) multiplexer_1 (
    .in0(soma_1_r0), .in1(\subtração_1_r0 ), .in2(\multiplicação_1_r0 ), .in3(\divisão_1_q0 ),
    .in4(\divisão_1_r0 ), .out({r7, r6, r5, r4, r3, r2, r1, r0}), .sel({s2, s1, s0}));  // open: in5, in6, in7
  Multiplexer #(.select(3), .enable("false")) multiplexer_2 (
    .in0(OverSoma), .in1(OverSub), .in2(OverMult), .in3(DivZero), .in4(DivZero), .out(overflow),
    .sel({s2, s1, s0}));  // open: in5, in6, in7

  // Other names for the same wires on the sheet: cl = Clock

  // Notes on the sheet:
  //   Analise do Overflow
endmodule

module Soma (
  input  a7,
  input  a6,
  input  a5,
  input  a4,
  input  a3,
  input  a2,
  input  a1,
  input  a0,
  input  b7,
  input  b6,
  input  b5,
  input  b4,
  input  b3,
  input  b2,
  input  b1,
  input  b0,
  output r7,
  output Overflow,
  output r6,
  output r5,
  output r4,
  output r3,
  output r2,
  output r1,
  output r0
);

  wire and_1_out, and_2_out, full_adder_2_carry_out, full_adder_3_carry_out, full_adder_4_carry_out,
       full_adder_5_carry_out, full_adder_6_carry_out, full_adder_7_carry_out, full_adder_8_carry_out;

  full_adder full_adder_1 (.X(b7), .Y(a7), .Sum(r7), .Carry_In(full_adder_2_carry_out));  // open: Carry_Out
  full_adder full_adder_2 (
    .X(b6), .Y(a6), .Sum(r6), .Carry_Out(full_adder_2_carry_out), .Carry_In(full_adder_3_carry_out));
  full_adder full_adder_3 (
    .X(b5), .Y(a5), .Sum(r5), .Carry_Out(full_adder_3_carry_out), .Carry_In(full_adder_4_carry_out));
  full_adder full_adder_4 (
    .X(b4), .Y(a4), .Sum(r4), .Carry_Out(full_adder_4_carry_out), .Carry_In(full_adder_5_carry_out));
  full_adder full_adder_5 (
    .X(b3), .Y(a3), .Sum(r3), .Carry_Out(full_adder_5_carry_out), .Carry_In(full_adder_6_carry_out));
  full_adder full_adder_6 (
    .X(b2), .Y(a2), .Sum(r2), .Carry_Out(full_adder_6_carry_out), .Carry_In(full_adder_7_carry_out));
  full_adder full_adder_7 (
    .X(b1), .Y(a1), .Sum(r1), .Carry_Out(full_adder_7_carry_out), .Carry_In(full_adder_8_carry_out));
  full_adder full_adder_8 (.X(b0), .Y(a0), .Sum(r0), .Carry_Out(full_adder_8_carry_out), .Carry_In(1'b0));
  and and_1 (and_1_out, a7, b7, ~r7);  // AND_Gate
  and and_2 (and_2_out, ~a7, ~b7, r7);  // AND_Gate
  or or_1 (Overflow, and_1_out, and_2_out);
endmodule

// FA
module full_adder (
  input  Carry_In,
  input  X,
  input  Y,
  output Sum,
  output Carry_Out
);

  wire and_1_out, and_2_out, xor_1_out;

  and and_1 (and_1_out, X, Y);
  xor xor_1 (xor_1_out, X, Y);
  or or_1 (Carry_Out, and_1_out, and_2_out);
  and and_2 (and_2_out, Carry_In, xor_1_out);
  xor xor_2 (Sum, Carry_In, xor_1_out);
endmodule

module \Subtração  (
  input  a7,
  input  a6,
  input  a5,
  input  a4,
  input  a3,
  input  a2,
  input  a1,
  input  a0,
  input  b7,
  input  b6,
  input  b5,
  input  b4,
  input  b3,
  input  b2,
  input  b1,
  input  b0,
  output r7,
  output r6,
  output r5,
  output r4,
  output r3,
  output r2,
  output r1,
  output r0,
  output Overflow
);

  wire complemento_de_dois_1_r0, complemento_de_dois_1_r1, complemento_de_dois_1_r2,
       complemento_de_dois_1_r3, complemento_de_dois_1_r4, complemento_de_dois_1_r5,
       complemento_de_dois_1_r6, complemento_de_dois_1_r7;

  complemento_de_dois complemento_de_dois_1 (
    .r7(complemento_de_dois_1_r7), .r6(complemento_de_dois_1_r6), .r5(complemento_de_dois_1_r5),
    .r4(complemento_de_dois_1_r4), .r3(complemento_de_dois_1_r3), .r2(complemento_de_dois_1_r2),
    .r1(complemento_de_dois_1_r1), .r0(complemento_de_dois_1_r0), .b7(b7), .b6(b6), .b5(b5), .b4(b4),
    .b3(b3), .b2(b2), .b1(b1), .b0(b0));
  Soma soma_1 (
    .r7(r7), .r6(r6), .r5(r5), .r4(r4), .r3(r3), .r2(r2), .r1(r1), .r0(r0), .a7(a7), .a6(a6), .a5(a5),
    .a4(a4), .a3(a3), .a2(a2), .a1(a1), .a0(a0), .b7(complemento_de_dois_1_r7),
    .b6(complemento_de_dois_1_r6), .b5(complemento_de_dois_1_r5), .b4(complemento_de_dois_1_r4),
    .b3(complemento_de_dois_1_r3), .b2(complemento_de_dois_1_r2), .b1(complemento_de_dois_1_r1),
    .b0(complemento_de_dois_1_r0), .Overflow(Overflow));
endmodule

// Complemento\n de dois
module complemento_de_dois (
  input  b7,
  input  b6,
  input  b5,
  input  b4,
  input  b3,
  input  b2,
  input  b1,
  input  b0,
  output r7,
  output r6,
  output r5,
  output r4,
  output r3,
  output r2,
  output r1,
  output r0
);

  wire not_1_out, not_2_out, not_3_out, not_4_out, not_5_out, not_6_out, not_7_out, not_8_out;

  not not_1 (not_1_out, b6);
  not not_2 (not_2_out, b7);
  not not_3 (not_3_out, b4);
  not not_4 (not_4_out, b5);
  Soma soma_1 (
    .r7(r7), .r6(r6), .r5(r5), .r4(r4), .r3(r3), .r2(r2), .r1(r1), .r0(r0), .a7(not_2_out), .a6(not_1_out),
    .a5(not_4_out), .a4(not_3_out), .a3(not_6_out), .a2(not_5_out), .a1(not_7_out), .a0(not_8_out),
    .b7(1'b0), .b6(1'b0), .b5(1'b0), .b4(1'b0), .b3(1'b0), .b2(1'b0), .b1(1'b0), .b0(1'b1));  // open: Overflow
  not not_5 (not_5_out, b2);
  not not_6 (not_6_out, b3);
  not not_7 (not_7_out, b1);
  not not_8 (not_8_out, b0);
endmodule

module \Multiplicação  (
  input  b7,
  input  b6,
  input  b5,
  input  b4,
  input  b3,
  input  b2,
  input  b1,
  input  b0,
  input  Clock,
  input  a7,
  input  a6,
  input  a5,
  input  a4,
  input  a3,
  input  a2,
  input  a1,
  input  a0,
  output r7,
  output r6,
  output r5,
  output r4,
  output r3,
  output r2,
  output r1,
  output r0,
  output Overflow
);

  wire bit_numero_1_r0, bit_numero_1_r1, bit_numero_1_r2, bit_numero_1_r3, bit_numero_1_r4, bit_numero_1_r5,
       bit_numero_1_r6, bit_numero_1_r7, \end , \módulo_1_r0 , \módulo_1_r1 , \módulo_1_r2 , \módulo_1_r3 ,
       \módulo_1_r4 , \módulo_1_r5 , \módulo_1_r6 , \módulo_1_r7 , \módulo_2_r0 , \módulo_2_r1 ,
       \módulo_2_r2 , \módulo_2_r3 , \módulo_2_r4 , \módulo_2_r5 , \módulo_2_r6 , \módulo_2_r7 , nor_1_out,
       not_1_out, not_2_out, reset, soma_1_overflow, xor_1_out;
  wire [7:0] and_2_out, cont, register_1_q, register_2_q, register_3_q, register_4_q, soma_1_r0, xnor_1_out,
       xnor_2_out, xnor_3_out;

  not not_1 (not_1_out, \end );
  bit___numero bit_numero_1 (
    .\bit (not_1_out), .b7(register_2_q[7]), .b6(register_2_q[6]), .b5(register_2_q[5]),
    .b4(register_2_q[4]), .b3(register_2_q[3]), .b2(register_2_q[2]), .b1(register_2_q[1]),
    .b0(register_2_q[0]), .r7(bit_numero_1_r7), .r6(bit_numero_1_r6), .r5(bit_numero_1_r5),
    .r4(bit_numero_1_r4), .r3(bit_numero_1_r3), .r2(bit_numero_1_r2), .r1(bit_numero_1_r1),
    .r0(bit_numero_1_r0));
  Soma soma_1 (
    .r7(soma_1_r0[7]), .r6(soma_1_r0[6]), .r5(soma_1_r0[5]), .r4(soma_1_r0[4]), .r3(soma_1_r0[3]),
    .r2(soma_1_r0[2]), .r1(soma_1_r0[1]), .r0(soma_1_r0[0]), .a7(bit_numero_1_r7), .a6(bit_numero_1_r6),
    .a5(bit_numero_1_r5), .a4(bit_numero_1_r4), .a3(bit_numero_1_r3), .a2(bit_numero_1_r2),
    .a1(bit_numero_1_r1), .a0(bit_numero_1_r0), .b7(\módulo_1_r7 ), .b6(\módulo_1_r6 ), .b5(\módulo_1_r5 ),
    .b4(\módulo_1_r4 ), .b3(\módulo_1_r3 ), .b2(\módulo_1_r2 ), .b1(\módulo_1_r1 ), .b0(\módulo_1_r0 ),
    .Overflow(soma_1_overflow));
  \módulo  \módulo_1  (
    .r7(\módulo_1_r7 ), .r6(\módulo_1_r6 ), .r5(\módulo_1_r5 ), .r4(\módulo_1_r4 ), .r3(\módulo_1_r3 ),
    .r2(\módulo_1_r2 ), .r1(\módulo_1_r1 ), .r0(\módulo_1_r0 ), .b7(a7), .b6(a6), .b5(a5), .b4(a4), .b3(a3),
    .b2(a2), .b1(a1), .b0(a0), .Oposto__caso_1__faz___a(1'b0));
  Register #(.trigger("high")) register_1 (.D(soma_1_r0), .Q(register_1_q), .clk(Clock));  // open: en, clr
  Register #(.trigger("high")) register_2 (
    .D(register_1_q), .Q(register_2_q), .clk(nor_1_out), .clr(reset));  // open: en
  assign xnor_1_out = ~(cont ^ {b7, b6, b5, b4, b3, b2, b1, b0});  // XNOR_Gate xnor_1, 8 bits wide
  S_R_Flip_Flop #(.trigger("falling")) s_r_ff_1 (
    .S(soma_1_overflow), .clk(Clock), .R(1'b0), .Q(Overflow), .reset(reset));  // open: Qn, preset, en
  xor xor_1 (xor_1_out, a7, b7);
  Counter counter_1 (.load(b7), .count(nor_1_out), .Q(cont), .clk(Clock), .clr(reset));  // open: D, carry
  and and_1 (\end , xnor_1_out[7], xnor_1_out[6], xnor_1_out[5], xnor_1_out[4], xnor_1_out[3], xnor_1_out[2], xnor_1_out[1], xnor_1_out[0]);
  \módulo  \módulo_2  (
    .r7(\módulo_2_r7 ), .r6(\módulo_2_r6 ), .r5(\módulo_2_r5 ), .r4(\módulo_2_r4 ), .r3(\módulo_2_r3 ),
    .r2(\módulo_2_r2 ), .r1(\módulo_2_r1 ), .r0(\módulo_2_r0 ), .b7(register_2_q[7]), .b6(register_2_q[6]),
    .b5(register_2_q[5]), .b4(register_2_q[4]), .b3(register_2_q[3]), .b2(register_2_q[2]),
    .b1(register_2_q[1]), .b0(register_2_q[0]), .Oposto__caso_1__faz___a(xor_1_out));
  bit___numero bit_numero_2 (
    .\bit (not_2_out), .b7(\módulo_2_r0 ), .b6(\módulo_2_r1 ), .b5(\módulo_2_r2 ), .b4(\módulo_2_r3 ),
    .b3(\módulo_2_r4 ), .b2(\módulo_2_r5 ), .b1(\módulo_2_r6 ), .b0(\módulo_2_r7 ), .r7(r0), .r6(r1),
    .r5(r2), .r4(r3), .r3(r4), .r2(r5), .r1(r6), .r0(r7));
  not not_2 (not_2_out, reset);
  nor nor_1 (nor_1_out, \end , Clock);
  nand nand_1 (reset, and_2_out[0], and_2_out[1], and_2_out[2], and_2_out[3], and_2_out[4], and_2_out[5], and_2_out[6], and_2_out[7]);
  assign and_2_out = xnor_2_out & xnor_3_out;  // AND_Gate and_2, 8 bits wide
  assign xnor_2_out = ~({b7, b6, b5, b4, b3, b2, b1, b0} ^ register_3_q);  // XNOR_Gate xnor_2, 8 bits wide
  Register register_3 (.D({b7, b6, b5, b4, b3, b2, b1, b0}), .Q(register_3_q), .clk(Clock));  // open: en, clr
  assign xnor_3_out = ~({a7, a6, a5, a4, a3, a2, a1, a0} ^ register_4_q);  // XNOR_Gate xnor_3, 8 bits wide
  Register register_4 (.D({a7, a6, a5, a4, a3, a2, a1, a0}), .Q(register_4_q), .clk(Clock));  // open: en, clr

  // Other names for the same wires on the sheet: cl = Clock

  // Notes on the sheet:
  //   bit * numero
  //   Contador
  //   bit * numero
  //   Produto
  //   Reset
endmodule

// Modulo
module \módulo  (
  input  Oposto__caso_1__faz___a,
  input  b7,
  input  b6,
  input  b5,
  input  b4,
  input  b3,
  input  b2,
  input  b1,
  input  b0,
  output r7,
  output r6,
  output r5,
  output r4,
  output r3,
  output r2,
  output r1,
  output r0
);

  wire not_1_out, xor_1_out;
  wire [7:0] complemento_de_dois_1_r0;

  complemento_de_dois complemento_de_dois_1 (
    .r7(complemento_de_dois_1_r0[7]), .r6(complemento_de_dois_1_r0[6]), .r5(complemento_de_dois_1_r0[5]),
    .r4(complemento_de_dois_1_r0[4]), .r3(complemento_de_dois_1_r0[3]), .r2(complemento_de_dois_1_r0[2]),
    .r1(complemento_de_dois_1_r0[1]), .r0(complemento_de_dois_1_r0[0]), .b7(b7), .b6(b6), .b5(b5), .b4(b4),
    .b3(b3), .b2(b2), .b1(b1), .b0(b0));
  xor xor_1 (xor_1_out, not_1_out, Oposto__caso_1__faz___a);
  not not_1 (not_1_out, b7);
  Multiplexer #(.width(8), .disabled(0), .enable("false")) multiplexer_1 (
    .in0(complemento_de_dois_1_r0), .in1({b7, b6, b5, b4, b3, b2, b1, b0}),
    .out({r7, r6, r5, r4, r3, r2, r1, r0}), .sel(xor_1_out));
endmodule

module bit___numero (
  input  b7,
  input  b6,
  input  b5,
  input  b4,
  input  b3,
  input  b2,
  input  b1,
  input  b0,
  input  \bit ,
  output r7,
  output r6,
  output r5,
  output r4,
  output r3,
  output r2,
  output r1,
  output r0
);

  and and_1 (r7, \bit , b7);
  and and_2 (r6, \bit , b6);
  and and_3 (r4, \bit , b4);
  and and_4 (r5, \bit , b5);
  and and_5 (r3, \bit , b3);
  and and_6 (r2, \bit , b2);
  and and_7 (r1, \bit , b1);
  and and_8 (r0, \bit , b0);
endmodule

module \Divisão  (
  input  a7,
  input  a6,
  input  a5,
  input  a4,
  input  a3,
  input  a2,
  input  a1,
  input  a0,
  input  Clock,
  input  b7,
  input  b6,
  input  b5,
  input  b4,
  input  b3,
  input  b2,
  input  b1,
  input  b0,
  output \Divisão_por_zero ,
  output r7,
  output r6,
  output r5,
  output r4,
  output r3,
  output r2,
  output r1,
  output r0,
  output q7,
  output q6,
  output q5,
  output q4,
  output q3,
  output q2,
  output q1,
  output q0
);

  wire bit_numero_1_r0, bit_numero_1_r1, bit_numero_1_r2, bit_numero_1_r3, bit_numero_1_r4, bit_numero_1_r5,
       bit_numero_1_r6, bit_numero_1_r7, bit_numero_2_r0, bit_numero_2_r1, bit_numero_2_r2, bit_numero_2_r3,
       bit_numero_2_r4, bit_numero_2_r5, bit_numero_2_r6, bit_numero_2_r7, \end , nand_1_out, nor_2_out,
       not_1_out, reset, sinais_diferentes;
  wire [7:0] and_2_out, \begin , bit_extender_1_out, mod_A, or_1_out, quo, register_1_q, register_3_q,
       register_4_q, register_5_q, resto_1_resto_final, resto_atual, \subtração_1_r0 , xnor_1_out, xnor_2_out;

  xor xor_1 (sinais_diferentes, a7, b7);
  bit___numero bit_numero_1 (
    .\bit (Clock), .b7(or_1_out[7]), .b6(or_1_out[6]), .b5(or_1_out[5]), .b4(or_1_out[4]), .b3(or_1_out[3]),
    .b2(or_1_out[2]), .b1(or_1_out[1]), .b0(or_1_out[0]), .r7(bit_numero_1_r7), .r6(bit_numero_1_r6),
    .r5(bit_numero_1_r5), .r4(bit_numero_1_r4), .r3(bit_numero_1_r3), .r2(bit_numero_1_r2),
    .r1(bit_numero_1_r1), .r0(bit_numero_1_r0));
  assign or_1_out = \begin  | resto_atual;  // OR_Gate or_1, 8 bits wide
  \Subtração  \subtração_1  (
    .a7(bit_numero_1_r7), .a6(bit_numero_1_r6), .a5(bit_numero_1_r5), .a4(bit_numero_1_r4),
    .a3(bit_numero_1_r3), .a2(bit_numero_1_r2), .a1(bit_numero_1_r1), .a0(bit_numero_1_r0),
    .b7(bit_numero_2_r0), .b6(bit_numero_2_r1), .b5(bit_numero_2_r2), .b4(bit_numero_2_r3),
    .b3(bit_numero_2_r4), .b2(bit_numero_2_r5), .b1(bit_numero_2_r6), .b0(bit_numero_2_r7),
    .r7(\subtração_1_r0 [7]), .r6(\subtração_1_r0 [6]), .r5(\subtração_1_r0 [5]), .r4(\subtração_1_r0 [4]),
    .r3(\subtração_1_r0 [3]), .r2(\subtração_1_r0 [2]), .r1(\subtração_1_r0 [1]), .r0(\subtração_1_r0 [0]));  // open: Overflow
  bit___numero bit_numero_2 (
    .\bit (Clock), .b7(b0), .b6(b1), .b5(b2), .b4(b3), .b3(b4), .b2(b5), .b1(b6), .b0(b7),
    .r7(bit_numero_2_r7), .r6(bit_numero_2_r6), .r5(bit_numero_2_r5), .r4(bit_numero_2_r4),
    .r3(bit_numero_2_r3), .r2(bit_numero_2_r2), .r1(bit_numero_2_r1), .r0(bit_numero_2_r0));
  not not_1 (not_1_out, reset);
  \módulo  \módulo_1  (
    .r7(mod_A[7]), .r6(mod_A[6]), .r5(mod_A[5]), .r4(mod_A[4]), .r3(mod_A[3]), .r2(mod_A[2]), .r1(mod_A[1]),
    .r0(mod_A[0]), .b7(a7), .b6(a6), .b5(a5), .b4(a4), .b3(a3), .b2(a2), .b1(a1), .b0(a0),
    .Oposto__caso_1__faz___a(b7));
  xor xor_2 (\end , register_1_q[7], b7);
  resto resto_1 (
    .Resto_atual(resto_atual), .B({b7, b6, b5, b4, b3, b2, b1, b0}), .Sinais_diferentes(sinais_diferentes),
    .Resto_final(resto_1_resto_final));
  bit___numero bit_numero_3 (
    .\bit (not_1_out), .b7(resto_1_resto_final[7]), .b6(resto_1_resto_final[6]), .b5(resto_1_resto_final[5]),
    .b4(resto_1_resto_final[4]), .b3(resto_1_resto_final[3]), .b2(resto_1_resto_final[2]),
    .b1(resto_1_resto_final[1]), .b0(resto_1_resto_final[0]), .r7(r7), .r6(r6), .r5(r5), .r4(r4), .r3(r3),
    .r2(r2), .r1(r1), .r0(r0));
  Register #(.trigger("high")) register_1 (.D(\subtração_1_r0 ), .Q(register_1_q), .clk(Clock));  // open: en, clr
  nor nor_1 (\Divisão_por_zero , b7, b6, b5, b4, b3, b2, b1, b0);
  Register #(.trigger("high")) register_2 (
    .D(register_1_q), .Q(resto_atual), .clk(nor_2_out), .clr(reset));  // open: en
  quociente quociente_1 (
    .\Divisão_acabou (\end ), .Resto(resto_1_resto_final), .Mesmo_sinal(sinais_diferentes), .Contador(quo),
    .q7(q7), .q6(q6), .q5(q5), .q4(q4), .q3(q3), .q2(q2), .q1(q1), .q0(q0));
  Register register_3 (.D(bit_extender_1_out), .Q(register_3_q), .clk(Clock));  // open: en, clr
  assign bit_extender_1_out = {{7{reset}}, reset};  // Bit_Extender bit_extender_1
  assign \begin  = register_3_q & mod_A;  // AND_Gate and_1, 8 bits wide
  Counter counter_1 (.count(nor_2_out), .Q(quo), .clk(Clock), .clr(reset));  // open: load, D, carry
  assign xnor_1_out = ~({b7, b6, b5, b4, b3, b2, b1, b0} ^ register_4_q);  // XNOR_Gate xnor_1, 8 bits wide
  Register register_4 (.D({b7, b6, b5, b4, b3, b2, b1, b0}), .Q(register_4_q), .clk(Clock));  // open: en, clr
  nor nor_2 (nor_2_out, \end , Clock);
  or or_2 (reset, nand_1_out, \Divisão_por_zero );
  nand nand_1 (nand_1_out, and_2_out[0], and_2_out[1], and_2_out[2], and_2_out[3], and_2_out[4], and_2_out[5], and_2_out[6], and_2_out[7]);
  assign and_2_out = xnor_1_out & xnor_2_out;  // AND_Gate and_2, 8 bits wide
  assign xnor_2_out = ~({a7, a6, a5, a4, a3, a2, a1, a0} ^ register_5_q);  // XNOR_Gate xnor_2, 8 bits wide
  Register register_5 (.D({a7, a6, a5, a4, a3, a2, a1, a0}), .Q(register_5_q), .clk(Clock));  // open: en, clr

  // Other names for the same wires on the sheet: cl = Clock; DivZero = \Divisão_por_zero 

  // Notes on the sheet:
  //   bit * numero
  //   bit * numero
  //   Corpo principal
  //   Análise dos sinais
  //   bit * numero
  //   Resto
  //   Quociente
  //   Passa o valor de A somente uma vez
  //   Contador
  //   Reset
endmodule

// Resto
module resto (
  input  Sinais_diferentes,
  input  [7:0] Resto_atual,
  input  [7:0] B,
  output [7:0] Resto_final
);

  wire [7:0] \subtração_1_r0 ;

  \Subtração  \subtração_1  (
    .a7(B[7]), .a6(B[6]), .a5(B[5]), .a4(B[4]), .a3(B[3]), .a2(B[2]), .a1(B[1]), .a0(B[0]),
    .b7(Resto_atual[7]), .b6(Resto_atual[6]), .b5(Resto_atual[5]), .b4(Resto_atual[4]), .b3(Resto_atual[3]),
    .b2(Resto_atual[2]), .b1(Resto_atual[1]), .b0(Resto_atual[0]), .r7(\subtração_1_r0 [7]),
    .r6(\subtração_1_r0 [6]), .r5(\subtração_1_r0 [5]), .r4(\subtração_1_r0 [4]), .r3(\subtração_1_r0 [3]),
    .r2(\subtração_1_r0 [2]), .r1(\subtração_1_r0 [1]), .r0(\subtração_1_r0 [0]));  // open: Overflow
  Multiplexer #(.width(8), .enable("false")) multiplexer_1 (
    .in0(Resto_atual), .in1(\subtração_1_r0 ), .out(Resto_final), .sel(Sinais_diferentes));
endmodule

// Quociente
module quociente (
  input  [7:0] Contador,
  input  \Divisão_acabou ,
  input  [7:0] Resto,
  input  Mesmo_sinal,
  output q7,
  output q6,
  output q5,
  output q4,
  output q3,
  output q2,
  output q1,
  output q0
);

  wire multiplexer_1_out, or_1_out, soma_1_r0, soma_1_r1, soma_1_r2, soma_1_r3, soma_1_r4, soma_1_r5,
       soma_1_r6, soma_1_r7;
  wire [7:0] complemento_de_dois_1_r0, multiplexer_2_out;

  Multiplexer #(.enable("false")) multiplexer_1 (.in0(1'b0), .in1(1'b1), .out(multiplexer_1_out), .sel(or_1_out));
  or or_1 (or_1_out, Resto[7], Resto[6], Resto[5], Resto[4], Resto[3], Resto[2], Resto[1], Resto[0]);
  Multiplexer #(.width(8), .enable("false")) multiplexer_2 (
    .in0(Contador), .in1({8{1'b0}}), .out(multiplexer_2_out), .sel(\Divisão_acabou ));
  Soma soma_1 (
    .r7(soma_1_r7), .r6(soma_1_r6), .r5(soma_1_r5), .r4(soma_1_r4), .r3(soma_1_r3), .r2(soma_1_r2),
    .r1(soma_1_r1), .r0(soma_1_r0), .a7(multiplexer_2_out[7]), .a6(multiplexer_2_out[6]),
    .a5(multiplexer_2_out[5]), .a4(multiplexer_2_out[4]), .a3(multiplexer_2_out[3]),
    .a2(multiplexer_2_out[2]), .a1(multiplexer_2_out[1]), .a0(multiplexer_2_out[0]), .b7(1'b0), .b6(1'b0),
    .b5(1'b0), .b4(1'b0), .b3(1'b0), .b2(1'b0), .b1(1'b0), .b0(multiplexer_1_out));  // open: Overflow
  complemento_de_dois complemento_de_dois_1 (
    .r7(complemento_de_dois_1_r0[7]), .r6(complemento_de_dois_1_r0[6]), .r5(complemento_de_dois_1_r0[5]),
    .r4(complemento_de_dois_1_r0[4]), .r3(complemento_de_dois_1_r0[3]), .r2(complemento_de_dois_1_r0[2]),
    .r1(complemento_de_dois_1_r0[1]), .r0(complemento_de_dois_1_r0[0]), .b7(soma_1_r7), .b6(soma_1_r6),
    .b5(soma_1_r5), .b4(soma_1_r4), .b3(soma_1_r3), .b2(soma_1_r2), .b1(soma_1_r1), .b0(soma_1_r0));
  Multiplexer #(.width(8), .enable("false")) multiplexer_3 (
    .in0(Contador), .in1(complemento_de_dois_1_r0), .out({q7, q6, q5, q4, q3, q2, q1, q0}), .sel(Mesmo_sinal));

  // Other names for the same wires on the sheet: quo[7:0] = Contador
endmodule
