// Logisim project ep3.circ as structural Verilog: 2 circuits, main circuit main
module main (
);

  wire cl, clock_1_out, d_ff_1_qn, JMP, not_1_out, or_1_out, STP, super_decodificador_1_lda,
       super_decodificador_1_sta, xor_1_out;
  wire [7:0] \Endereço , IR__Instruction_Register_q, multiplexer_1_out, PC__Program_counter_q;
  wire [15:0] ACC, demultiplexer_1_out0, demultiplexer_1_out1, ram_1_data;

  Clock #(.highDuration(2), .lowDuration(2)) clock_1 (.out(clock_1_out));
  D_Flip_Flop d_ff_1 (.clk(clock_1_out), .Qn(d_ff_1_qn));  // open: D, Q, preset, en, reset
  not not_1 (not_1_out, clock_1_out);
  ExactlyOne xor_1 (.out(xor_1_out), .in0(STP), .in1(JMP), .in2(d_ff_1_qn));
  Clock clock_2 (.out(cl));
  Counter PC__Program_counter (
    .load(JMP), .D(\Endereço ), .count(xor_1_out), .Q(PC__Program_counter_q), .clk(not_1_out));  // open: carry, clr
  Multiplexer #(.width(8), .enable("false")) multiplexer_1 (
    .in0(PC__Program_counter_q), .in1(\Endereço ), .out(multiplexer_1_out), .sel(or_1_out));
  or or_1 (or_1_out, super_decodificador_1_sta, super_decodificador_1_lda);
  Demultiplexer #(.width(16), .enable("false")) demultiplexer_1 (
    .out0(demultiplexer_1_out0), .out1(demultiplexer_1_out1), .in(ram_1_data), .sel(super_decodificador_1_lda));
  RAM #(.dataWidth(16), .bus("separate")) ram_1 (
    .addr(multiplexer_1_out), .din(ACC), .data(ram_1_data), .str(super_decodificador_1_sta), .clk(cl));  // open: sel, ld, clr
  // Probe on IR__Instruction_Register_q
  Super_Decodificador super_decodificador_1 (
    .in_1(IR__Instruction_Register_q), .LDA(super_decodificador_1_lda), .STA(super_decodificador_1_sta),
    .JMP(JMP), .STP(STP));  // open: NOP
  // Probe on demultiplexer_1_out1
  Register #(.width(16)) IR__Instruction_Register (
    .D(demultiplexer_1_out0), .Q({IR__Instruction_Register_q, \Endereço }), .clk(cl));  // open: en, clr
  // Probe on \Endereço 
  Register #(.width(16), .trigger("falling")) Acumulador (
    .D(demultiplexer_1_out1), .en(super_decodificador_1_lda), .Q(ACC), .clk(cl));  // open: clr

  // Notes on the sheet:
  //   Memória
endmodule

// Decodificador
module Super_Decodificador (
  input  [7:0] in_1,
  output LDA,
  output STA,
  output NOP,
  output JMP,
  output STP
);

  wire _0, _2, _3L, _3R, _4L, _6, B, C;

  and and_1 (LDA, _0, B);
  and and_2 (STA, _0, C);
  Decoder #(.select(4), .enable("false")) decoder_1 (
    .out0(_0), .out3(_3L), .out4(_4L), .sel(in_1[7:4]));  // open: out1, out2, out5, out6, out7, out8, out9, out10, out11, out12, out13, out14, out15
  and and_3 (JMP, _3L, _3R);
  and and_4 (NOP, _3L, _2);
  and and_5 (STP, _4L, _6);
  Decoder #(.select(4), .enable("false")) decoder_2 (
    .out2(_2), .out3(_3R), .out6(_6), .out11(B), .out12(C), .sel(in_1[3:0]));  // open: out0, out1, out4, out5, out7, out8, out9, out10, out13, out14, out15

  // Notes on the sheet:
  //   Analisa código hexadecimal
endmodule
